# Fritzing sketch simple-sensor-setup (saved by Fritzing 0.9.4)
breadboards: 1

parts:
  Bauteil1 = Arduino Nano (Rev3.0)
  Bauteil2 = Soil Moisture Sensor
  Part1 = KY-019 5V Relay Module [package="Breakout board"]
  U1 = LM2596 step down module
  OLED1 = OLED 128x64 I2C Monochrome Display
  JACK1 = 2.1mm Barrel Jack with Terminal Block

nets:
  GND: Bauteil1.GND, Bauteil2.GND, Part1.-, U1.IN-, U1.OUT-, OLED1.GND, JACK1.POS
  N1: Bauteil1.D7, Part1.S
  N2: Bauteil1.A4, Bauteil2.SIG
  3V3: Bauteil1.3V3, OLED1.VDD
  N3: Part1.+, U1.OUT+
  N4: U1.IN+, JACK1.NEG

notes:
  12V DC

custom parts:
  KY-019 5V Relay Module: KY-019 5V Relay module, used to control AC circuits.
  LM2596 step down module: LM2596 DC-DC step down power supply module 3 A.
